# Fritzing sketch wiring_fritzing (saved by Fritzing 1.0.3b)
breadboards: 1

parts:
  Bauteil1 = Arduino Mega 2560 (Rev3)
  Flowmeter = mystery part, 3 pins [chip_label=?]
  S5 = Pushbutton [package=THT]
  S6 = Pushbutton [package=THT]
  S7 = Pushbutton [package=THT]
  S8 = Pushbutton [package=THT]
  8_Channel_Relay1 = 8 Channel Power Relay
  LCD1 = LCD screen  # not connected
  Grove1 = Grove OLED 128x96
  M1 = MW-IRM-03-5 [part_number=IRM]

nets:
  N1: Bauteil1.D21/SCL, Grove1.SCL
  N2: Bauteil1.D20/SDA, Grove1.SDA
  N3: Bauteil1.D11_PWM, S8.leg1
  N4: Bauteil1.D10_PWM, S7.leg1
  N5: Bauteil1.D9_PWM, S6.leg1
  N6: Bauteil1.D8_PWM, S5.leg1
  VCC: Bauteil1.5V, Flowmeter.pin3, 8_Channel_Relay1.VCC, 8_Channel_Relay1.JD-VCC, Grove1.VCC, M1.+Vo
  GND: Bauteil1.GND, Flowmeter.pin2, S5.leg0, S6.leg0, S7.leg0, S8.leg0, 8_Channel_Relay1.GND, Grove1.GND, M1.-Vo
  N7: Bauteil1.D2_PWM, Flowmeter.pin1
  N8: Bauteil1.D22, 8_Channel_Relay1.IN1
  N9: 8_Channel_Relay1.COM, M1.AC/L

notes:
  Ventil

custom parts:
  8 Channel Power Relay: An 8 channel power relay. The module operates at 5V.
  MW-IRM-03-5: AC-DC 220V to 5V Step-Down Power Supply Module
